# Fritzing sketch TeensyChordPlayerBreadboardSketch (saved by Fritzing 0.9.3b)
circuit board: 8.46667cm x 5.64444cm
breadboards: 1

parts:
  Teensy_3_1 = Teensy 3.1
  S1 = SWITCH-MOMENTARY-2 [package=tactile-pth-12mm]
  S2 = SWITCH-MOMENTARY-2 [package=tactile-pth-12mm]
  S3 = SWITCH-MOMENTARY-2 [package=tactile-pth-12mm]
  S4 = SWITCH-MOMENTARY-2 [package=tactile-pth-12mm]
  R1 = Rotary Potentiometer (Small) [maximum_resistance=100kΩ package=THT]
  R2 = Rotary Potentiometer (Small) [maximum_resistance=100kΩ package=THT]
  R3 = Rotary Potentiometer (Small) [maximum_resistance=100kΩ package=THT]

nets:
  N1: Teensy_3_1.D3, S1.1
  N2: Teensy_3_1.D4, S2.1
  N3: Teensy_3_1.D5, S3.1
  N4: Teensy_3_1.D6, S4.1
  N5: Teensy_3_1.A0/D14, R3.wiper
  N6: Teensy_3_1.A1/D15, R2.wiper
  N7: Teensy_3_1.A2/D16, R1.wiper
  N8: Teensy_3_1.3V3, R1.leg2, R2.leg2, R3.leg2
  N9: Teensy_3_1.AGND, S1.2, S2.2, S3.2, S4.2, R1.leg1, R2.leg1, R3.leg1
